# Fritzing sketch diagramaRFID (saved by Fritzing 0.8.7b)
breadboards: 1

parts:
  UNO = Arduino Uno (Rev3)
  RC522 = RFID-RC522-v2
  Relay = Keyes Relay [package=THT]
  R1 = Resistor [tolerance=±5% resistance=220 package=THT]
  R2 = Resistor [tolerance=±5% resistance=220 package=THT]
  R3 = Resistor [tolerance=±5% resistance=220 package=THT]
  LED1 = LED - 5mm [color="Red (633nm)" package="5 mm [THT]"]
  LED2 = LED - 5mm [color="Green (570nm)" package="5 mm [THT]"]
  LED3 = LED - 5mm [color="Blue (505nm)" package="5 mm [THT]"]
  S1 = Pushbutton [package="[THT]"]

nets:
  N1: UNO.D9_PWM, RC522.RST
  N2: UNO.D10_PWM/SS, RC522.SDA
  N3: UNO.D11_PWM/MOSI, RC522.MOSI
  N4: UNO.D12/MISO, RC522.MISO
  N5: UNO.D13/SCK, RC522.SCK
  N6: UNO.D3_PWM, S1.Pin_1, S1.Pin_2
  N7: UNO.D4, Relay.signal
  N8: UNO.D5_PWM, LED3.anode
  N9: UNO.D6_PWM, LED2.anode
  N10: UNO.D7, LED1.anode
  3V3: UNO.3V3, RC522.3.3V
  N11: UNO.5V, Relay.power, R3.Pin_1
  N12: UNO.GND, R1.Pin_1, R2.Pin_1
  N13: RC522.GND, Relay.ground, S1.Pin_3, S1.Pin_4
  N14: R1.Pin_0, LED1.cathode
  N15: R2.Pin_0, LED2.cathode
  N16: R3.Pin_0, LED3.cathode

custom parts:
  RFID-RC522-v2: A simple China made RFID-RC522 Reader; do check the pin labels, as this is a MFRC522 based clone.
  Keyes Relay: The Keyes 5V relay module is suitable for SCM development, home appliance control. It uses a 5V~12V TIL control signal which can control DC / AC signal.
